# Fritzing sketch LUX_tsl2561 (saved by Fritzing 0.9.10b)
breadboards: 1

parts:
  Part1 = Adafruit TSL2561 [part_number="Adafruit #439"]
  Mod1 = Amica NodeMCU DEVKIT 1.0

nets:
  N1: Part1.GND, Mod1.pin2, Mod1.pin_9
  N2: Part1.3.3V, Mod1.pin1, Mod1.pin_10
  N3: Part1.SDA, Mod1.pin_12
  N4: Part1.SCL, Mod1.pin_13

custom parts:
  Adafruit TSL2561: The TSL2561 luminosity sensor is an advanced digital light sensor, ideal for use in a wide range of light situations. Compared to low cost CdS cells, this sensor is more precise, allowing for exact lux calculations and can be configured for different gain/timing ranges to detect light ranges from up to 0.1 - 40,000+ Lux on the fly. The best part of this sensor is that it contains both infrared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
